# Fritzing sketch psens (saved by Fritzing 0.9.2b)
circuit board: 8.46667cm x 5.64444cm
breadboards: 1

parts:
  Arduino = Arduino Nano (Rev3.0)
  R1 = Resistor [tolerance=±5% resistance=220 package=THT]
  R2 = Resistor [tolerance=±5% resistance=220 package=THT]
  R3 = Resistor [tolerance=±5% resistance=220 package=THT]
  LED1 = smd LED [color="Red (633nm)" package="1206 [SMD]"]
  LED2 = smd LED [color="Red (633nm)" package="1206 [SMD]"]
  LED3 = smd LED [color="Red (633nm)" package="1206 [SMD]"]
  HC_Sensor = SRF05 Ultrasonic Rangefinder

nets:
  GND: Arduino.GND, R1.Pin_1, R2.Pin_1, R3.Pin_1, HC_Sensor.GND
  N1: Arduino.D2, LED1.cathode
  N2: Arduino.D3, LED2.cathode
  N3: Arduino.D4, LED3.cathode
  N4: Arduino.D11/MOSI, HC_Sensor.Echo
  N5: Arduino.D12/MISO, HC_Sensor.Trig
  5V: Arduino.5V, HC_Sensor.VCC
  N6: R1.Pin_0, LED3.anode
  N7: R2.Pin_0, LED2.anode
  N8: R3.Pin_0, LED1.anode

// code stored in the sketch: psens.ino
#include <NewPing.h>

#define R_LED 2
#define Y_LED 3
#define G_LED 4
#define ECHO_PIN     11
#define TRIGGER_PIN  12
#define MAX_DISTANCE 500
#define DELAY 10

struct history {
  unsigned int cur;
  unsigned int hist[100];
  unsigned int hsize;
  history(unsigned int hsize = 10) : 
  cur(0), hist({
    0  }
  ),hsize(hsize) {
  }
  void add(int i){
    hist[cur] = i;
    cur = (cur + 1) % hsize;  
  }
  int avg(){
    int sum = 0;
    int divider = hsize;
    for (int i = 0; i < hsize; i++) {
      if (hist[i%hsize] == 0) {
        divider--;        
      }
      else{
        sum = sum + hist[i%hsize];      
      }
    }
    return sum / divider;
  }
};

NewPing sonar(TRIGGER_PIN,ECHO_PIN,MAX_DISTANCE);
history *h = new history(50);

void setup(){
  pinMode(R_LED, OUTPUT);
  pinMode(G_LED, OUTPUT);
  pinMode(Y_LED, OUTPUT);
  //Serial.begin(115200);
}

void loop(){
  delay(DELAY);
  h->add(sonar.ping_cm());
  int distance = h->avg();
  //Serial.print(distance);
  //Serial.println(" cm");


  if (distance == -1){
    nothing(); 
  }
  else if (distance > 100){
    green();  
  }
  else if (distance > 5){
    yellow();   
  }
  else{
    red();     
  }
}

void nothing() {
  digitalWrite(G_LED, HIGH);
  digitalWrite(Y_LED, HIGH);  
  digitalWrite(R_LED, HIGH);
}

void green(){
  digitalWrite(G_LED, HIGH);
  digitalWrite(Y_LED, LOW);  
  digitalWrite(R_LED, LOW);
}

void yellow(){
  digitalWrite(G_LED, LOW);
  digitalWrite(Y_LED, HIGH);  
  digitalWrite(R_LED, LOW);
}

void red(){
  digitalWrite(G_LED, LOW);
  digitalWrite(Y_LED, LOW);  
  digitalWrite(R_LED, HIGH);
}
